# Fritzing sketch Sketch (saved by Fritzing 1.0.1rc)

parts:
  R1 = Resistor [tolerance=±5% resistance=330 package="2010 [SMD]"]
  C3 = Electrolytic Capacitor [capacitance=1μF voltage=6.3V package="0405 [SMD, electrolytic]"]
  M2 = STM32F103C8T6 blue mini board
  VCC2 = 4 x AAA Battery Mount
  U1 = WS2812 RGB LED strip

nets:
  N1: R1.Pin_0, M2.A1
  N2: R1.Pin_1, U1.DIN
  N3: C3.-, M2.G, VCC2.-, U1.GND
  N4: C3.+, VCC2.+, U1.VCC

custom parts:
  WS2812 RGB LED strip: WS2812 strip
